# Fritzing sketch LazyCouch (saved by Fritzing 0.7.11b)
breadboards: 1

parts:
  Arduino_Ethernet_Shield1 = Arduino Ethernet Shield  # not connected
  J1 = Basic Force Sensing Resistor (FSR) [package=THT]
  R1 = Resistor [tolerance=±5% resistance=1k package=THT]
  S1 = Pushbutton [package="[THT]"]
  R2 = Resistor [tolerance=±5% resistance=10k package=THT]
  LED1 = LED - 5mm [color="Green (565nm)" package="5 mm [THT]"]
  R3 = Resistor [tolerance=±5% resistance=220 package=THT]

nets:
  N1: J1.pin_0, R1.Pin_0
  N2: J1.pin_1, S1.Pin_1, S1.Pin_2
  N3: R1.Pin_1, R2.Pin_1, LED1.cathode
  N4: S1.Pin_3, S1.Pin_4, R2.Pin_0
  N5: LED1.anode, R3.Pin_0
